// Digital circuit componente.dig as structural Verilog
module componente (
  input  e2,
  input  e1,
  input  e0,
  output S
);

  wire and_1_out, overflow_1_ov, xor_1_out;

  overflow overflow_1 (.A_n_1(and_1_out), .B_n_1(xor_1_out), .S_n_1(xor_1_out), .Ov(overflow_1_ov));
  and and_1 (and_1_out, e2, ~e1);  // And
  xor xor_1 (xor_1_out, e1, e0);
  or or_1 (S, ~overflow_1_ov, xor_1_out);  // Or
endmodule
