// Digital circuit micircuito1.dig as structural Verilog
module micircuito1 (
  input  e2,
  input  e1,
  input  e0,
  output S
);

  wire gen_ov_s_1_p1, gen_ov_s_1_p2, gen_ov_s_1_p4;

  // gen_ov_s gen_ov_s_1: pin names not known; wires that end beside it: gen_ov_s_1_p1, gen_ov_s_1_p2, gen_ov_s_1_p2, gen_ov_s_1_p4
  and and_1 (gen_ov_s_1_p1, e2, ~e1);  // And
  xor xor_1 (gen_ov_s_1_p2, e1, e0);
  or or_1 (S, ~gen_ov_s_1_p4, gen_ov_s_1_p2);  // Or

  // Notes on the sheet:
  //   e2: default 1
  //   e0: default 1
endmodule
