// Digital circuit Eje2_circuito2.dig as structural Verilog
module Eje2_circuito2 (
  input  e2,
  input  e1,
  input  e0,
  output s
);

  wire nand_1_out;

  nand nand_1 (nand_1_out, e2, e1);
  or or_1 (s, nand_1_out, e0);
endmodule
